# Fritzing sketch Kidbright (saved by Fritzing 0.9.3b)

parts:
  BAT1 = Battery Holders [package=battery-aa]
  M1 = DC Motor
  M2 = DC Motor
  BRD1 = KidBright32 [package=breakout]
  S1 = H-Bridge with L298N
  BAT2 = Battery Holders [package=battery-aa]
  BAT3 = Battery Holders [package=battery-aa]
  BAT4 = Battery Holders [package=battery-aa]
  BAT5 = Battery Holders [package=battery-aa]
  BAT6 = Battery Holders [package=battery-aa]
  BAT7 = Battery Holders [package=battery-aa]
  BAT8 = Battery Holders [package=battery-aa]
  J1 = Power Jack [package=power_jack_slot]
  S2 = Toggle Switch [package=THT]
  R1 = Resistor [tolerance=±5% resistance=10 package="2010 [SMD]"]

nets:
  N1: BAT1.-, S2.COM
  N2: BAT1.+, BAT2.-
  N3: M1.pin_1, S1.M2-02
  N4: M1.pin_2, S1.M2-01
  N5: M2.pin_1, S1.M1-02
  N6: M2.pin_2, S1.M1-01
  N7: BRD1.J1_1, S1.5V
  N8: BRD1.J1_3, S1.ENA
  N9: BRD1.J1_4, S1.ENB
  N10: BRD1.J1_5, S1.IN3
  N11: BRD1.J1_6, S1.IN4
  GND: BRD1.J1_8, S1.GND, BAT6.+, J1.GNDBREAK, J1.GND
  N12: BRD1.J6_6, S1.IN2
  N13: BRD1.J6_7, S1.IN1
  N14: S1.12V, S2.L1
  N15: BAT2.+, BAT4.-
  N16: BAT3.-, BAT4.+
  N17: BAT3.+, BAT5.-
  N18: BAT5.+, BAT7.-
  N19: BAT6.-, BAT8.+
  N20: BAT7.+, BAT8.-
  N21: J1.PWR, R1.Pin_1
  N22: S2.L2, R1.Pin_0

notes:
  FLIP FLOP
  Switch Chose
  - Charger DC12V
  - Run KidBright

custom parts:
  KidBright32: KidBright32 Board
  H-Bridge with L298N: h-bridge

// code stored in the sketch: FlipFlop.ino
/*
  Flip Flop
  switching between two LEDs using a button
  
  This example is part of the Fritzing Creator Kit: www.fritzing.org/creator-kit.
*/

int buttonPin=2;                       // Pin where the button is attached
int greenLED=9;                        // Pin where the green LED is attached
int redLED=10;                         // Pin where the red LED is attached 

void setup(){
  pinMode(buttonPin, INPUT);           // button is initialised as INPUT 
  pinMode(greenLED, OUTPUT);           // green LED pin is initialised as OUTPUT 
  pinMode(redLED, OUTPUT);             // red LED pin is initialised as OUTPUT  
}

void loop(){
  if (digitalRead(buttonPin)==LOW){    // if the button is pressed (LOW) 
    digitalWrite(greenLED, HIGH);      // switch on green LED
    digitalWrite(redLED, LOW);         // switch off red LED
  } else {                             // else (if button is not pressed)
    digitalWrite(greenLED, LOW);       // switch off green LED
    digitalWrite(redLED, HIGH);        // switch on red LED
  }
}

// code stored in the sketch: Workshop_01_Blink.ino
int led = 13;

void setup() {
  pinMode(led, OUTPUT);
}
void loop() {
  digitalWrite(led, HIGH);
  delay(1000);
  digitalWrite(led, LOW);
  delay(1000);
}
